// Logisim project cpu.circ as structural Verilog
module alu (
  input  [15:0] Source,
  input  [15:0] Destination,
  input  [3:0] Op,
  output [15:0] Out,
  output Zero
);

  wire [15:0] adder_1_out, adder_2_out, nand_1_out, negator_1_out, shifter_1_out, shifter_2_out,
       subtractor_1_out, subtractor_2_out;

  Shifter #(.width(16), .shift("lr")) shifter_1 (.in(Source), .\dist (4'b0001), .out(shifter_1_out));
  Shifter #(.width(16)) shifter_2 (.in(Source), .\dist (4'b0001), .out(shifter_2_out));
  Adder #(.width(16)) adder_1 (.a(Destination), .b(Source), .out(adder_1_out), .cin(1'b0));  // open: cout
  Subtractor #(.width(16)) subtractor_1 (
    .a(Destination), .b(Source), .out(subtractor_1_out), .bin(1'b0));  // open: bout
  assign nand_1_out = ~(Destination & Source);  // NAND_Gate nand_1, 16 bits wide
  Negator #(.width(16)) negator_1 (.in(Source), .out(negator_1_out));
  Adder #(.width(16)) adder_2 (.a(Source), .b(16'h1), .out(adder_2_out));  // open: cin, cout
  Subtractor #(.width(16)) subtractor_2 (.a(Source), .b(16'h1), .out(subtractor_2_out));  // open: bin, bout
  Multiplexer #(.select(4), .width(16), .enable("false")) multiplexer_1 (
    .in0(shifter_1_out), .in1(shifter_2_out), .in2(adder_1_out), .in3(subtractor_1_out), .in4(nand_1_out),
    .in5(negator_1_out), .in6({16{1'b0}}), .in7(16'h1), .in8(Source), .in9(adder_2_out),
    .in10(subtractor_2_out), .out(Out), .sel(Op));  // open: in11, in12, in13, in14, in15
  nor nor_1 (Zero, 1'b0, Out[15], Out[14], Out[13], Out[12], Out[11], Out[10], Out[9], Out[8], Out[7], Out[6], Out[5], Out[4], Out[3], Out[2], Out[1], Out[0]);
endmodule

module register_bank (
  input  WEn,
  input  [15:0] DstIn,
  input  Clk,
  input  [2:0] DstSel,
  input  [2:0] SrcSel,
  output [15:0] DstOut,
  output [15:0] SrcOut
);

  wire demultiplexer_1_out0, demultiplexer_1_out1, demultiplexer_1_out2, demultiplexer_1_out3,
       demultiplexer_1_out4, demultiplexer_1_out5, demultiplexer_1_out6, demultiplexer_1_out7, not_1_out;
  wire [15:0] register_1_q, register_2_q, register_3_q, register_4_q, register_5_q, register_6_q,
       register_7_q, register_8_q;

  not not_1 (not_1_out, WEn);
  Demultiplexer #(.select(3)) demultiplexer_1 (
    .out0(demultiplexer_1_out0), .out1(demultiplexer_1_out1), .out2(demultiplexer_1_out2),
    .out3(demultiplexer_1_out3), .out4(demultiplexer_1_out4), .out5(demultiplexer_1_out5),
    .out6(demultiplexer_1_out6), .out7(demultiplexer_1_out7), .in(not_1_out), .sel(DstSel));  // open: en
  Multiplexer #(.select(3), .width(16)) multiplexer_1 (
    .in0(register_1_q), .in1(register_2_q), .in2(register_3_q), .in3(register_4_q), .in4(register_5_q),
    .in5(register_6_q), .in6(register_7_q), .in7(register_8_q), .out(DstOut), .sel(DstSel));  // open: en
  Register #(.width(16)) register_1 (.D(DstIn), .en(demultiplexer_1_out0), .Q(register_1_q), .clk(Clk));  // open: clr
  Multiplexer #(.select(3), .width(16)) multiplexer_2 (
    .in0(register_1_q), .in1(register_2_q), .in2(register_3_q), .in3(register_4_q), .in4(register_5_q),
    .in5(register_6_q), .in6(register_7_q), .in7(register_8_q), .out(SrcOut), .sel(SrcSel));  // open: en
  Register #(.width(16)) register_2 (.D(DstIn), .en(demultiplexer_1_out1), .Q(register_2_q), .clk(Clk));  // open: clr
  Register #(.width(16)) register_3 (.D(DstIn), .en(demultiplexer_1_out2), .Q(register_3_q), .clk(Clk));  // open: clr
  Register #(.width(16)) register_4 (.D(DstIn), .en(demultiplexer_1_out3), .Q(register_4_q), .clk(Clk));  // open: clr
  Register #(.width(16)) register_5 (.D(DstIn), .en(demultiplexer_1_out4), .Q(register_5_q), .clk(Clk));  // open: clr
  Register #(.width(16)) register_6 (.D(DstIn), .en(demultiplexer_1_out5), .Q(register_6_q), .clk(Clk));  // open: clr
  Register #(.width(16)) register_7 (.D(DstIn), .en(demultiplexer_1_out6), .Q(register_7_q), .clk(Clk));  // open: clr
  Register #(.width(16)) register_8 (.D(DstIn), .en(demultiplexer_1_out7), .Q(register_8_q), .clk(Clk));  // open: clr
endmodule
